# Fritzing sketch circuitoLDR (saved by Fritzing 0.9.3b)
breadboards: 1

parts:
  FR1 = Franzininho
  R1 = Photocell (LDR) [package=THT]
  R2 = Resistor [tolerance=±5% resistance=10k package=THT]

nets:
  N1: FR1.GND, R1.pin_0
  N2: FR1.VCC, R2.Pin_1
  N3: R1.pin_1, R2.Pin_0

custom parts:
  Franzininho: A Franzininho é uma placa com ATtiny85 compatível com o Arduino Gemma. Ela foi desenvolvida com objetivo de promover a inclusão no mundo da eletrônica e programação. O circuito em face simples e com componentes PTHs, facilita o uso da placa em oficinas de solda. Por ser compatível com a plataforma Arduino, pode ela também pode ser usada para atividades de programação tanto para iniciantes como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
